// Logisim project LP_02.circ as structural Verilog: 5 circuits, main circuit 1bit adder
module _1bit_adder (
  input  B0,
  input  A0,
  input  Ci,
  output S0,
  output Cout
);

  wire and_1_out, and_2_out, xor_1_out;

  xor xor_1 (xor_1_out, A0, B0);
  and and_1 (and_1_out, A0, B0);
  xor xor_2 (S0, xor_1_out, Ci);
  and and_2 (and_2_out, xor_1_out, Ci);
  or or_1 (Cout, and_2_out, and_1_out);
endmodule

module Mux_S1 (
  input  A0,
  input  B0,
  input  S0,
  output out_4
);

  wire and_1_out, and_2_out, not_1_out;

  not not_1 (not_1_out, S0);
  and and_1 (and_1_out, S0, B0);
  and and_2 (and_2_out, not_1_out, A0);
  or or_1 (out_4, and_1_out, and_2_out);
endmodule

module Mux_S2 (
  input  in_1,
  input  in_2,
  input  in_3,
  input  in_4,
  input  in_5,
  input  in_6,
  output out_7
);

  wire and_1_out, and_2_out, and_3_out, and_4_out, not_1_out, not_2_out, not_3_out, not_4_out;

  not not_1 (not_1_out, in_6);
  not not_2 (not_2_out, in_5);
  not not_3 (not_3_out, in_6);
  not not_4 (not_4_out, in_5);
  and and_1 (and_1_out, in_4, not_1_out, not_2_out);
  and and_2 (and_2_out, in_3, not_3_out, in_5);
  and and_3 (and_3_out, in_2, in_6, not_4_out);
  and and_4 (and_4_out, in_1, in_6, in_5);
  or or_1 (out_7, and_1_out, and_2_out, and_3_out, and_4_out);
endmodule

module ULA_1Bit (
  input  E1,
  input  E0,
  input  S1,
  input  S0,
  input  BiVert,
  input  Ci,
  output S,
  output Cout
);

  wire and_1_out, mux_s1_1_out_4, n1bit_adder_1_s0, not_1_out, not_2_out, or_1_out;

  not not_1 (not_1_out, E1);
  Mux_S1 mux_s1_1 (.out_4(mux_s1_1_out_4), .A0(E1), .B0(not_1_out), .S0(BiVert));
  and and_1 (and_1_out, E0, mux_s1_1_out_4);
  or or_1 (or_1_out, E0, mux_s1_1_out_4);
  not not_2 (not_2_out, E0);
  _1bit_adder u_1bit_adder_1 (.S0(n1bit_adder_1_s0), .Cout(Cout), .B0(E0), .A0(mux_s1_1_out_4), .Ci(Ci));
  Mux_S2 mux_s2_1 (
    .out_7(S), .in_1(n1bit_adder_1_s0), .in_2(not_2_out), .in_3(or_1_out), .in_4(and_1_out), .in_5(S1),
    .in_6(S0));
endmodule

module main (
  input  BinVert,
  input  B3,
  input  B2,
  input  B1,
  input  B0,
  input  A3,
  input  A2,
  input  A1,
  input  A0,
  input  S1,
  input  S2,
  output s0,
  output s1_2,
  output s2_2,
  output s3,
  output Cout
);

  wire ula_1bit_1_cout, ula_1bit_2_cout, ula_1bit_3_cout;

  ULA_1Bit ula_1bit_1 (.S(s0), .E1(B0), .E0(A0), .Ci(1'b0), .BiVert(BinVert), .Cout(ula_1bit_1_cout), .S1(S1), .S0(S2));
  ULA_1Bit ula_1bit_2 (
    .S(s1_2), .E1(B1), .E0(A1), .Ci(ula_1bit_1_cout), .BiVert(BinVert), .Cout(ula_1bit_2_cout), .S1(S1),
    .S0(S2));
  ULA_1Bit ula_1bit_3 (
    .S(s2_2), .E1(B2), .E0(A2), .Ci(ula_1bit_2_cout), .BiVert(BinVert), .Cout(ula_1bit_3_cout), .S1(S1),
    .S0(S2));
  ULA_1Bit ula_1bit_4 (.S(s3), .E1(B3), .E0(A3), .Ci(ula_1bit_3_cout), .BiVert(BinVert), .Cout(Cout), .S1(S1), .S0(S2));
endmodule
